// Logisim project alu.circ as structural Verilog: 1 circuit, main circuit ALU
module ALU (
  input  [31:0] Input1,
  input  [31:0] Input2,
  input  [4:0] op,
  input  [4:0] SHA,
  output Zero,
  output [31:0] Result
);

  wire comparator_1_eq, comparator_1_lt, comparator_2_eq, comparator_2_gt, comparator_2_lt, not_1_out,
       or_2_out, or_3_out;
  wire [31:0] ADD, AND32, BEQ, BGEZ, BGTZ, BLEZ, BNE, DIV, MULT, NOR32, OR32, SL, SLT, SRArith, SRLog, SUB,
       XOR32;

  Adder #(.width(32)) adder_1 (.a(Input1), .b(Input2), .out(ADD));  // open: cin, cout
  Subtractor #(.width(32)) subtractor_1 (.a(Input1), .b(Input2), .out(SUB));  // open: bin, bout
  Multiplier #(.width(32)) multiplier_1 (.a(Input1), .b(Input2), .out(MULT));  // open: cin, cout
  Divider #(.width(32)) divider_1 (.a(Input1), .b(Input2), .out(DIV));  // open: upper, rem
  Shifter #(.width(32)) shifter_1 (.in(Input2), .\dist (SHA), .out(SL));
  Shifter #(.shift("lr"), .width(32)) shifter_2 (.in(Input2), .\dist (SHA), .out(SRLog));
  Shifter #(.shift("ar"), .width(32)) shifter_3 (.in(Input2), .\dist (SHA), .out(SRArith));
  assign OR32 = Input1 | Input2;  // OR_Gate or_1, 32 bits wide
  assign AND32 = Input1 & Input2;  // AND_Gate and_1, 32 bits wide
  assign XOR32 = Input1 ^ Input2;  // XOR_Gate xor_1, 32 bits wide
  assign NOR32 = ~(Input1 | Input2);  // NOR_Gate nor_1, 32 bits wide
  Comparator #(.width(32)) comparator_1 (
    .a(Input1), .b(Input2), .eq(comparator_1_eq), .lt(comparator_1_lt));  // open: gt
  Comparator #(.width(32)) comparator_2 (
    .a(Input1), .b({32{1'b0}}), .gt(comparator_2_gt), .eq(comparator_2_eq), .lt(comparator_2_lt));
  not not_1 (not_1_out, comparator_1_eq);
  assign BEQ = {{31{1'b0}}, comparator_1_eq};  // Bit_Extender bit_extender_1
  assign BNE = {{31{1'b0}}, not_1_out};  // Bit_Extender bit_extender_2
  assign SLT = {{31{1'b0}}, comparator_1_lt};  // Bit_Extender bit_extender_3
  assign BGTZ = {{31{1'b0}}, comparator_2_gt};  // Bit_Extender bit_extender_4
  assign BGEZ = {{31{1'b0}}, or_2_out};  // Bit_Extender bit_extender_5
  or or_2 (or_2_out, comparator_2_gt, comparator_2_eq);
  assign BLEZ = {{31{1'b0}}, or_3_out};  // Bit_Extender bit_extender_6
  or or_3 (or_3_out, comparator_2_eq, comparator_2_lt);
  Comparator #(.width(32)) comparator_3 (.a({32{1'b0}}), .b(Result), .eq(Zero));  // open: gt, lt
  Multiplexer #(.select(5), .width(32)) multiplexer_1 (
    .in0(ADD), .in1(ADD), .in2(SUB), .in3(SUB), .in4(AND32), .in5(OR32), .in6(NOR32), .in7(XOR32), .in8(SL),
    .in9(SRLog), .in10(SRArith), .in11(SLT), .in12(MULT), .in13(DIV), .in14(BEQ), .in15(BNE), .in16(BLEZ),
    .in17(BGTZ), .in18(BGEZ), .in19({32{1'b0}}), .in20({32{1'b0}}), .in21({32{1'b0}}), .in22({32{1'b0}}),
    .in23({32{1'b0}}), .in24({32{1'b0}}), .in25({32{1'b0}}), .in26({32{1'b0}}), .in27({32{1'b0}}),
    .in28({32{1'b0}}), .in29({32{1'b0}}), .in30({32{1'b0}}), .in31({32{1'b0}}), .out(Result), .sel(op));

  // Other names for the same wires on the sheet: ADDu[31:0] = ADD; in1[31:0] = Input1; in2[31:0] = Input2;
  //   res[31:0] = Result; SUBu[31:0] = SUB

  // Notes on the sheet:
  //   Inputs
  //   Outputs
endmodule
