// Logisim project alu_control.circ as structural Verilog: 1 circuit, main circuit alu_control_unit
module alu_control_unit (
  input  [5:0] func,
  input  [5:0] opcode,
  output [4:0] ALU_control_bits,
  output [1:0] Shift_Select
);

  wire comparator_1_eq, comparator_2_eq, not_1_out, not_2_out;
  wire [1:0] pla_3_out, pla_4_out;
  wire [4:0] pla_1_out, pla_2_out;

  PLA #(.in_width(6), .out_width(5), .\table ("100110 00111 # XOR\n000000 01000 # SLL\n000100 01000 # SLLV\n000010 01001 # SRL\n100010 00010 # SUB\n000110 01001 # SRLV\n101010 01011 # SLT\n100011 00011 # SUBu\n100101 00101 # OR\n100111 00110 # NOR\n100001 00001 # ADDu\n011000 01100 # MULT\n011010 01101 # DIV\n100100 00100 # AND\n100000 00000 # ADD\n001000 11111 # JR\n000011 01010 # SRA")) pla_1 (
    .in(func), .out(pla_1_out));
  PLA #(.in_width(6), .out_width(5), .\table ("001000 00000 # ADDi\n001001 00001 # ADDiu\n001100 00100 # ANDi\n001110 00111 # XORi\n001101 00101 # ORi\n000100 01110 # BEQ\n000101 01111 # BNE\n000110 10000 # BLEZ\n000111 10001 # BGTZ\n000001 10010 # BGEZ\n100011 00000 # LW\n101011 00000 # SW\n100000 00000 # LB\n101000 00000 # SB\n001010 01011 # SLTi\n001111 01000 # Lui\n000010 11111 # J\n000011 11111 # JAL")) pla_2 (
    .in(opcode), .out(pla_2_out));
  PLA #(.in_width(6), .\table ("000000 00 # SLL\n000100 01 # SLLV\n000010 00 # SRL\n000110 01 # SRLV\n000011 00 # SRA")) pla_3 (
    .in(func), .out(pla_3_out));
  PLA #(.in_width(6), .\table ("001111 10 # Lui")) pla_4 (.in(opcode), .out(pla_4_out));
  Comparator #(.width(6)) comparator_1 (.a(opcode), .b({6{1'b0}}), .eq(comparator_1_eq));  // open: gt, lt
  Comparator #(.width(6)) comparator_2 (.a(opcode), .b({6{1'b0}}), .eq(comparator_2_eq));  // open: gt, lt
  not not_1 (not_1_out, comparator_1_eq);
  not not_2 (not_2_out, comparator_2_eq);
  Multiplexer #(.width(5)) multiplexer_1 (.in0(pla_1_out), .in1(pla_2_out), .out(ALU_control_bits), .sel(not_1_out));
  Multiplexer #(.width(2)) multiplexer_2 (.in0(pla_3_out), .in1(pla_4_out), .out(Shift_Select), .sel(not_2_out));
endmodule
