// Logisim project cpu.circ as structural Verilog: 1 circuit, main circuit cpu
module cpu (
  output [31:0] out_1,
  output [31:0] out_2,
  output out_3,
  output out_4,
  output out_5,
  output [5:0] out_6,
  output out_7,
  output out_8
);

  wire ALU_Src_EX, ALU_Src_ID, ALU_Src_MEM, ALU_Src_WB, and_1_out, and_2_out, and_3_out, and_4_out,
       and_5_out, and_6_out, and_7_out, and_8_out, and_9_out, cache_1_wb_mask_select, comparator_1_eq,
       comparator_2_eq, comparator_3_eq, comparator_4_eq, Finish_EX, Finish_ID, Finish_MEM, Finish_WB,
       hit_MEM, hit_WB, is_branch_inst_EX, is_branch_inst_ID, is_branch_inst_IF, is_JR_ins_IF_used,
       is_JR_inst_IF, is_jump_inst_IF, is_mem_inst_EX, is_mem_inst_ID, is_mem_inst_MEM,
       is_mem_inst_MEM_secondary, is_mem_inst_WB, Is_Prediction_Incorrect_EX, mem_fetch_done, mem_mask_sel,
       multiplexer_8_out, multiplexer_9_out, multiplexer_21_out, multiplexer_22_out, multiplexer_32_out,
       multiplexer_33_out, multiplexer_38_out, multiplexer_41_out, not_1_out, not_2_out, not_3_out,
       not_6_out, not_7_out, not_8_out, not_9_out, not_10_out, or_1_out, or_2_out, or_3_out, or_4_out,
       Predict_Taken_EX, Predict_Taken_ID, Predict_Taken_IF, Predict_Taken_MEM, Predict_Taken_WB,
       Reg_Write_EX, Reg_Write_ID, Reg_Write_MEM, Reg_Write_WB, stall_by_JR, stall_counter_reset, Zero_EX,
       Zero_MEM, Zero_WB;
  wire [0:0] counter_2_q;
  wire [1:0] JR_stall_counter, mem_data_sel, MEMW_Sel_EX, MEMW_Sel_ID, MEMW_Sel_MEM, MEMW_Sel_WB,
       multiplexer_34_out, multiplexer_35_out, multiplexer_36_out, multiplexer_37_out, PC_control_EX,
       PC_control_ID, PC_control_MEM, PC_control_WB, Reg_Dest_EX, Reg_Dest_ID, Reg_Dest_MEM, Reg_Dest_WB,
       Reg_Write_Sel_EX, Reg_Write_Sel_ID, Reg_Write_Sel_MEM, Reg_Write_Sel_WB, Shift_Select;
  wire [2:0] mem_addr_sel;
  wire [3:0] decoder_1_out0, multiplexer_46_out, multiplexer_49_out;
  wire [4:0] ALU_Ctrl, multiplexer_13_out, multiplexer_14_out, multiplexer_16_out, multiplexer_17_out,
       multiplexer_20_out, multiplexer_26_out, multiplexer_27_out, multiplexer_29_out, multiplexer_30_out,
       multiplexer_45_out, rd_EX, rd_ID, rd_MEM, rd_WB, Reg_Write_Target_MEM, rs_EX, rs_ID, rs_MEM, rs_WB,
       rt_EX, rt_ID, rt_MEM, rt_WB, SHA_EX, SHA_ID, SHA_MEM, SHA_WB;
  wire [5:0] Func_EX, Func_ID, Func_IF, Func_MEM, Func_WB, multiplexer_12_out, multiplexer_15_out,
       multiplexer_25_out, multiplexer_28_out, opcode_EX, opcode_ID, opcode_IF, opcode_MEM, opcode_WB;
  wire [7:0] miss_counter_state;
  wire [25:6] J_addr;
  wire [31:0] ALU_Result_EX, ALU_Result_MEM, ALU_Result_WB, cache_1_fetch0_addr, cache_1_fetch1_addr,
       cache_1_fetch2_addr, cache_1_fetch3_addr, cache_1_write_back0_addr, cache_1_write_back0_data,
       cache_1_write_back1_addr, cache_1_write_back1_data, cache_1_write_back2_addr,
       cache_1_write_back2_data, cache_1_write_back3_addr, cache_1_write_back3_data, Imm_ext_EX, Imm_ext_ID,
       Imm_ext_IF, Imm_ext_MEM, Imm_ext_WB, J_value, MemReadData_MEM, MemReadData_WB, multiplexer_1_out,
       multiplexer_2_out, multiplexer_3_out, multiplexer_4_out, multiplexer_10_out, multiplexer_11_out,
       multiplexer_18_out, multiplexer_19_out, multiplexer_23_out, multiplexer_24_out, multiplexer_31_out,
       multiplexer_39_out, multiplexer_40_out, multiplexer_42_out, multiplexer_43_out, multiplexer_44_out,
       multiplexer_48_out, multiplexer_50_out, newPC, PC_4_IF, PC_4_Imm_IF, PC_4_Imm_MEM, PC_4_MEM, PC_EX,
       PC_ID, PC_IF, PC_MEM, PC_WB, Read_Data1_EX, Read_Data1_ID, Read_Data1_MEM, Read_Data1_WB,
       Read_Data2_EX, Read_Data2_ID, Read_Data2_MEM, Read_Data2_WB, Replace_Prediciton_EX,
       Replace_Prediciton_ID, Replace_Prediciton_IF, Replace_Prediciton_MEM, Replace_Prediciton_WB,
       shifter_1_out, shifter_3_out;

  not not_1 (not_1_out, Zero_EX);
  and and_1 (and_1_out, is_JR_inst_IF, stall_by_JR);
  not not_2 (not_2_out, is_JR_ins_IF_used);
  Shifter #(.width(32)) shifter_1 (.in(Imm_ext_IF), .\dist (5'b00010), .out(shifter_1_out));
  Counter #(.max('h1), .width(2)) counter_1 (
    .clr(stall_counter_reset), .load(1'b0), .up(1'b0), .clk(not_3_out), .Q(JR_stall_counter));  // open: count, D, carry
  not not_3 (not_3_out, out_5);
  and and_2 (and_2_out, is_JR_inst_IF, not_2_out);
  Multiplexer #(.width(32)) multiplexer_1 (
    .in0(PC_4_IF), .in1(PC_4_Imm_IF), .out(multiplexer_1_out), .sel(Predict_Taken_IF));
  Counter #(.max('h3), .ongoal("stay"), .width(2)) counter_2 (
    .up(not_1_out), .count(is_branch_inst_EX), .clk(out_5), .Q({Predict_Taken_IF, counter_2_q[0]}));  // open: clr, load, D, carry
  Comparator #(.width(2)) comparator_1 (.a(JR_stall_counter), .b(2'b00), .eq(comparator_1_eq));  // open: gt, lt
  or or_1 (or_1_out, and_1_out, and_2_out);
  Multiplexer #(.width(32)) multiplexer_2 (
    .in0(PC_4_IF), .in1(J_value), .out(multiplexer_2_out), .sel(is_jump_inst_IF));
  Multiplexer #(.width(32)) multiplexer_3 (
    .in0(multiplexer_1_out), .in1(Read_Data1_EX), .out(multiplexer_3_out), .sel(is_JR_inst_IF));
  Adder #(.width(32)) adder_1 (.a(PC_IF), .b(32'h4), .out(PC_4_IF));  // open: cin, cout
  Shifter #(.width(28)) shifter_2 (.in({2'b00, J_addr, Func_IF}), .\dist (5'b00010), .out(J_value[27:0]));
  PLA #(.in_width(12), .out_width(3), .\table ("xxxxxx001000 000 # ADDi\nxxxxxx001001 000 # ADDiu\nxxxxxx001100 000 # ANDi\nxxxxxx001110 000 # XORi\nxxxxxx001101 000 # ORi\nxxxxxx000100 010 # BEQ\nxxxxxx000101 010 # BNE\nxxxxxx000110 010 # BLEZ\nxxxxxx000111 010 # BGTZ\nxxxxxx000001 010 # BGEZ\nxxxxxx100011 000 # LW\nxxxxxx101011 000 # SW\nxxxxxx100000 001 # LB\nxxxxxx101000 000 # SB\nxxxxxx001010 000 # SLTi\nxxxxxx001111 000 # Lui\nxxxxxx000010 001 # J\nxxxxxx000011 001 # JAL\n100110000000 000 # XOR\n000000000000 000 # SLL\n000100000000 000 # SLLV\n000010000000 000 # SRL\n100010000000 000 # SUB\n000110000000 000 # SRLV\n101010000000 000 # SLT\n001100000000 000 # Syscall\n100011000000 000 # SUBu\n100101000000 000 # OR\n100111000000 000 # NOR\n100001000000 000 # ADDu\n011000000000 000 # MULT\n011010000000 000 # DIV\n100100000000 000 # AND\n100000000000 000 # ADD\n001000000000 100 # JR\n000011000000 000 # SRA")) pla_1 (
    .in({Func_IF, opcode_IF}), .out({is_JR_inst_IF, is_branch_inst_IF, is_jump_inst_IF}));
  Shifter #(.width(32)) shifter_3 (.in(Imm_ext_MEM), .\dist (5'b00010), .out(shifter_3_out));
  Adder #(.width(32)) adder_2 (.a(PC_IF), .b(32'h4), .out(PC_4_IF));  // open: cin, cout
  Adder #(.width(32)) adder_3 (.a(PC_4_IF), .b(shifter_1_out), .out(PC_4_Imm_IF));  // open: cin, cout
  not not_4 (stall_by_JR, comparator_1_eq);
  or or_2 (or_2_out, Finish_ID, or_1_out);
  Multiplexer #(.width(32)) multiplexer_4 (
    .in0(multiplexer_2_out), .in1(multiplexer_3_out), .out(multiplexer_4_out), .sel(or_3_out));
  or or_3 (or_3_out, is_branch_inst_IF, is_JR_inst_IF);
  Adder #(.width(32)) adder_4 (.a(PC_MEM), .b(32'h4), .out(PC_4_MEM));  // open: cin, cout
  Adder #(.width(32)) adder_5 (.a(PC_4_MEM), .b(shifter_3_out), .out(PC_4_Imm_MEM));  // open: cin, cout
  Register #(.width(32)) PC (.D(newPC), .en(stall_counter_reset), .clk(out_5), .Q(PC_IF));  // open: clr
  not not_5 (stall_counter_reset, or_2_out);
  Clock clock_1 (.out(out_4));
  Multiplexer #(.width(32)) multiplexer_5 (
    .in0(multiplexer_4_out), .in1(Replace_Prediciton_EX), .out(newPC), .sel(and_3_out));
  and and_3 (and_3_out, is_branch_inst_EX, Is_Prediction_Incorrect_EX);
  Multiplexer #(.width(32)) multiplexer_6 (
    .in0(PC_4_Imm_IF), .in1(PC_4_IF), .out(Replace_Prediciton_IF), .sel(Predict_Taken_IF));
  and and_4 (and_4_out, out_4, hit_MEM);
  and and_5 (and_5_out, is_JR_inst_IF, stall_by_JR);
  D_Flip_Flop #(.trigger("falling")) d_ff_1 (
    .D(and_5_out), .clk(out_5), .Q(is_JR_ins_IF_used));  // open: Qn, preset, reset
  Multiplexer multiplexer_7 (.in0(out_4), .in1(and_4_out), .out(out_5), .sel(is_mem_inst_MEM_secondary));
  mem InstMem (
    .MemAddress(PC_IF), .MemWriteMask(4'b0000), .MemWriteData({32{1'b1}}), .clk(out_5),
    .MemReadData({opcode_IF, J_addr, Func_IF}));
  assign Imm_ext_IF = {{16{J_addr[15]}}, {J_addr[15:6], Func_IF}};  // Bit_Extender bit_extender_1
  Register #(.width(1)) register_1 (.D(multiplexer_8_out), .en(1'b1), .clk(out_5), .Q(is_branch_inst_ID));  // open: clr
  Multiplexer multiplexer_8 (.in0(is_branch_inst_IF), .in1(1'b0), .out(multiplexer_8_out), .sel(or_4_out));
  Register #(.width(1)) register_2 (.D(multiplexer_9_out), .en(1'b1), .clk(out_5), .Q(Predict_Taken_ID));  // open: clr
  Multiplexer multiplexer_9 (.in0(Predict_Taken_IF), .in1(1'b0), .out(multiplexer_9_out), .sel(or_4_out));
  Register #(.width(32)) register_3 (
    .D(multiplexer_10_out), .en(1'b1), .clk(out_5), .Q(Replace_Prediciton_ID));  // open: clr
  Multiplexer #(.width(32)) multiplexer_10 (
    .in0(Replace_Prediciton_IF), .in1({32{1'b0}}), .out(multiplexer_10_out), .sel(or_4_out));
  Register #(.width(32)) register_4 (.D(multiplexer_11_out), .en(1'b1), .clk(out_5), .Q(PC_ID));  // open: clr
  Multiplexer #(.width(32)) multiplexer_11 (.in0(PC_IF), .in1({32{1'b0}}), .out(multiplexer_11_out), .sel(or_4_out));
  Register #(.width(6)) register_5 (.D(multiplexer_12_out), .en(1'b1), .clk(out_5), .Q(opcode_ID));  // open: clr
  Multiplexer #(.width(6)) multiplexer_12 (.in0(opcode_IF), .in1({6{1'b1}}), .out(multiplexer_12_out), .sel(or_4_out));
  Register #(.width(5)) register_6 (.D(multiplexer_13_out), .en(1'b1), .clk(out_5), .Q(rs_ID));  // open: clr
  Multiplexer #(.width(5)) multiplexer_13 (
    .in0(J_addr[25:21]), .in1({5{1'b0}}), .out(multiplexer_13_out), .sel(or_4_out));
  Register #(.width(5)) register_7 (.D(multiplexer_14_out), .en(1'b1), .clk(out_5), .Q(rt_ID));  // open: clr
  Multiplexer #(.width(5)) multiplexer_14 (
    .in0(J_addr[20:16]), .in1({5{1'b0}}), .out(multiplexer_14_out), .sel(or_4_out));
  Register #(.width(6)) register_8 (.D(multiplexer_15_out), .en(1'b1), .clk(out_5), .Q(Func_ID));  // open: clr
  Multiplexer #(.width(6)) multiplexer_15 (.in0(Func_IF), .in1({6{1'b1}}), .out(multiplexer_15_out), .sel(or_4_out));
  Register #(.width(5)) register_9 (.D(multiplexer_16_out), .en(1'b1), .clk(out_5), .Q(SHA_ID));  // open: clr
  Multiplexer #(.width(5)) multiplexer_16 (
    .in0(J_addr[10:6]), .in1({5{1'b0}}), .out(multiplexer_16_out), .sel(or_4_out));
  Register #(.width(5)) register_10 (.D(multiplexer_17_out), .en(1'b1), .clk(out_5), .Q(rd_ID));  // open: clr
  Multiplexer #(.width(5)) multiplexer_17 (
    .in0(J_addr[15:11]), .in1({5{1'b0}}), .out(multiplexer_17_out), .sel(or_4_out));
  Register #(.width(32)) register_11 (.D(multiplexer_18_out), .en(1'b1), .clk(out_5), .Q(Imm_ext_ID));  // open: clr
  Multiplexer #(.width(32)) multiplexer_18 (
    .in0(Imm_ext_IF), .in1({32{1'b0}}), .out(multiplexer_18_out), .sel(or_4_out));
  and and_6 (and_6_out, Is_Prediction_Incorrect_EX, is_branch_inst_EX);
  Comparator #(.width(32)) comparator_2 (.a(PC_IF), .b({32{1'b0}}), .eq(comparator_2_eq));  // open: gt, lt
  or or_4 (or_4_out, and_6_out, stall_by_JR, comparator_2_eq);
  Multiplexer #(.select(2), .width(32)) multiplexer_19 (
    .in0(ALU_Result_WB), .in1(MemReadData_WB), .in2(PC_WB), .in3({{24{1'b0}}, MemReadData_WB[7:0]}),
    .out(multiplexer_19_out), .sel(Reg_Write_Sel_WB));
  PLA #(.in_width(6), .out_width(1), .\table ("100011 1 # LW\n100000 1 # LB\n101000 1 # SB\n101011 1 # SW")) Checker (
    .in(opcode_ID), .out(is_mem_inst_ID));
  Multiplexer #(.select(2), .width(5)) multiplexer_20 (
    .in0(rt_WB), .in1(rd_WB), .in2({5{1'b1}}), .in3(5'b00001), .out(multiplexer_20_out), .sel(Reg_Dest_WB));
  // control_unit CU: pin names not known; wires that end beside it: opcode_ID, Func_ID, Reg_Write_ID, ALU_Src_ID, PC_control_ID, Reg_Dest_ID, Reg_Write_Sel_ID, MEMW_Sel_ID, Finish_ID
  // regfile RegisterFile: pin names not known; wires that end beside it: rs_ID, rt_ID, multiplexer_20_out, multiplexer_19_out, Reg_Write_WB, out_5, Read_Data1_ID, Read_Data2_ID
  Multiplexer multiplexer_21 (.in0(is_branch_inst_ID), .in1(1'b0), .out(multiplexer_21_out), .sel(and_7_out));
  Multiplexer multiplexer_22 (.in0(Predict_Taken_ID), .in1(1'b0), .out(multiplexer_22_out), .sel(and_7_out));
  Multiplexer #(.width(32)) multiplexer_23 (
    .in0(Replace_Prediciton_ID), .in1({32{1'b0}}), .out(multiplexer_23_out), .sel(and_7_out));
  Multiplexer #(.width(32)) multiplexer_24 (.in0(PC_ID), .in1({32{1'b0}}), .out(multiplexer_24_out), .sel(and_7_out));
  Multiplexer #(.width(6)) multiplexer_25 (.in0(opcode_ID), .in1({6{1'b1}}), .out(multiplexer_25_out), .sel(and_7_out));
  Multiplexer #(.width(5)) multiplexer_26 (.in0(rs_ID), .in1({5{1'b0}}), .out(multiplexer_26_out), .sel(and_7_out));
  Multiplexer #(.width(5)) multiplexer_27 (.in0(rt_ID), .in1({5{1'b0}}), .out(multiplexer_27_out), .sel(and_7_out));
  Multiplexer #(.width(6)) multiplexer_28 (.in0(Func_ID), .in1({6{1'b1}}), .out(multiplexer_28_out), .sel(and_7_out));
  Multiplexer #(.width(5)) multiplexer_29 (.in0(SHA_ID), .in1({5{1'b0}}), .out(multiplexer_29_out), .sel(and_7_out));
  Multiplexer #(.width(5)) multiplexer_30 (.in0(rd_ID), .in1({5{1'b0}}), .out(multiplexer_30_out), .sel(and_7_out));
  Multiplexer #(.width(32)) multiplexer_31 (
    .in0(Imm_ext_ID), .in1({32{1'b0}}), .out(multiplexer_31_out), .sel(and_7_out));
  Multiplexer multiplexer_32 (.in0(Reg_Write_ID), .in1(1'b0), .out(multiplexer_32_out), .sel(and_7_out));
  Multiplexer multiplexer_33 (.in0(ALU_Src_ID), .in1(1'b1), .out(multiplexer_33_out), .sel(and_7_out));
  Multiplexer #(.width(2)) multiplexer_34 (.in0(PC_control_ID), .in1(2'b11), .out(multiplexer_34_out), .sel(and_7_out));
  Multiplexer #(.width(2)) multiplexer_35 (.in0(Reg_Dest_ID), .in1(2'b11), .out(multiplexer_35_out), .sel(and_7_out));
  Multiplexer #(.width(2)) multiplexer_36 (
    .in0(Reg_Write_Sel_ID), .in1(2'b11), .out(multiplexer_36_out), .sel(and_7_out));
  Multiplexer #(.width(2)) multiplexer_37 (.in0(MEMW_Sel_ID), .in1(2'b11), .out(multiplexer_37_out), .sel(and_7_out));
  Multiplexer multiplexer_38 (.in0(Finish_ID), .in1(1'b0), .out(multiplexer_38_out), .sel(and_7_out));
  Multiplexer #(.width(32)) multiplexer_39 (
    .in0(Read_Data1_ID), .in1({32{1'b1}}), .out(multiplexer_39_out), .sel(and_7_out));
  Multiplexer #(.width(32)) multiplexer_40 (
    .in0(Read_Data2_ID), .in1({32{1'b1}}), .out(multiplexer_40_out), .sel(and_7_out));
  Multiplexer multiplexer_41 (.in0(is_mem_inst_ID), .in1(1'b0), .out(multiplexer_41_out), .sel(and_7_out));
  and and_7 (and_7_out, Is_Prediction_Incorrect_EX, is_branch_inst_EX);
  Register #(.width(1)) register_12 (
    .D(multiplexer_21_out), .en(1'b1), .clk(out_5), .Q(is_branch_inst_EX));  // open: clr
  Register #(.width(1)) register_13 (
    .D(multiplexer_22_out), .en(1'b1), .clk(out_5), .Q(Predict_Taken_EX));  // open: clr
  Register #(.width(32)) register_14 (
    .D(multiplexer_23_out), .en(1'b1), .clk(out_5), .Q(Replace_Prediciton_EX));  // open: clr
  Register #(.width(32)) register_15 (.D(multiplexer_24_out), .en(1'b1), .clk(out_5), .Q(PC_EX));  // open: clr
  Register #(.width(6)) register_16 (.D(multiplexer_25_out), .en(1'b1), .clk(out_5), .Q(opcode_EX));  // open: clr
  Register #(.width(5)) register_17 (.D(multiplexer_26_out), .en(1'b1), .clk(out_5), .Q(rs_EX));  // open: clr
  Register #(.width(5)) register_18 (.D(multiplexer_27_out), .en(1'b1), .clk(out_5), .Q(rt_EX));  // open: clr
  Register #(.width(6)) register_19 (.D(multiplexer_28_out), .en(1'b1), .clk(out_5), .Q(Func_EX));  // open: clr
  Register #(.width(5)) register_20 (.D(multiplexer_29_out), .en(1'b1), .clk(out_5), .Q(SHA_EX));  // open: clr
  Register #(.width(5)) register_21 (.D(multiplexer_30_out), .en(1'b1), .clk(out_5), .Q(rd_EX));  // open: clr
  Register #(.width(32)) register_22 (.D(multiplexer_31_out), .en(1'b1), .clk(out_5), .Q(Imm_ext_EX));  // open: clr
  Register #(.width(1)) register_23 (.D(multiplexer_32_out), .en(1'b1), .clk(out_5), .Q(Reg_Write_EX));  // open: clr
  Register #(.width(1)) register_24 (.D(multiplexer_33_out), .en(1'b1), .clk(out_5), .Q(ALU_Src_EX));  // open: clr
  Register #(.width(2)) register_25 (.D(multiplexer_34_out), .en(1'b1), .clk(out_5), .Q(PC_control_EX));  // open: clr
  Register #(.width(2)) register_26 (.D(multiplexer_35_out), .en(1'b1), .clk(out_5), .Q(Reg_Dest_EX));  // open: clr
  Register #(.width(2)) register_27 (
    .D(multiplexer_36_out), .en(1'b1), .clk(out_5), .Q(Reg_Write_Sel_EX));  // open: clr
  Register #(.width(2)) register_28 (.D(multiplexer_37_out), .en(1'b1), .clk(out_5), .Q(MEMW_Sel_EX));  // open: clr
  Register #(.width(1)) register_29 (.D(multiplexer_38_out), .en(1'b1), .clk(out_5), .Q(Finish_EX));  // open: clr
  Register #(.width(32)) register_30 (.D(multiplexer_39_out), .en(1'b1), .clk(out_5), .Q(Read_Data1_EX));  // open: clr
  Register #(.width(32)) register_31 (.D(multiplexer_40_out), .en(1'b1), .clk(out_5), .Q(Read_Data2_EX));  // open: clr
  Register #(.width(1)) register_32 (.D(multiplexer_41_out), .en(1'b1), .clk(out_5), .Q(is_mem_inst_EX));  // open: clr
  Comparator #(.width(5)) comparator_3 (.a(rt_EX), .b(Reg_Write_Target_MEM), .eq(comparator_3_eq));  // open: gt, lt
  Multiplexer #(.width(32)) multiplexer_42 (
    .in0(Read_Data1_EX), .in1(ALU_Result_MEM), .out(multiplexer_42_out), .sel(comparator_4_eq));
  Comparator #(.width(5)) comparator_4 (.a(rs_EX), .b(Reg_Write_Target_MEM), .eq(comparator_4_eq));  // open: gt, lt
  Multiplexer #(.width(32)) multiplexer_43 (
    .in0(Read_Data2_EX), .in1(ALU_Result_MEM), .out(multiplexer_43_out), .sel(comparator_3_eq));
  Multiplexer #(.width(32)) multiplexer_44 (
    .in0(multiplexer_43_out), .in1(Imm_ext_EX), .out(multiplexer_44_out), .sel(ALU_Src_EX));
  not not_6 (not_6_out, Zero_EX);
  Multiplexer #(.select(2), .width(5)) multiplexer_45 (
    .in0(SHA_EX), .in1(Read_Data1_EX[4:0]), .in2(5'b10000), .in3({5{1'b0}}), .out(multiplexer_45_out),
    .sel(Shift_Select));
  xor xor_1 (Is_Prediction_Incorrect_EX, Predict_Taken_EX, not_6_out);
  // alu_control_unit ALU_Control: pin names not known; wires that end beside it: Func_EX, opcode_EX, ALU_Ctrl, Shift_Select
  // ALU ArithLogicUnit: pin names not known; wires that end beside it: multiplexer_42_out, multiplexer_44_out, ALU_Ctrl, multiplexer_45_out, Zero_EX, ALU_Result_EX
  Register #(.width(1)) register_33 (.D(Predict_Taken_EX), .en(1'b1), .clk(out_5), .Q(Predict_Taken_MEM));  // open: clr
  Register #(.width(32)) register_34 (
    .D(Replace_Prediciton_EX), .en(1'b1), .clk(out_5), .Q(Replace_Prediciton_MEM));  // open: clr
  Register #(.width(32)) register_35 (.D(PC_EX), .en(1'b1), .clk(out_5), .Q(PC_MEM));  // open: clr
  Register #(.width(6)) register_36 (.D(opcode_EX), .en(1'b1), .clk(out_5), .Q(opcode_MEM));  // open: clr
  Register #(.width(5)) register_37 (.D(rs_EX), .en(1'b1), .clk(out_5), .Q(rs_MEM));  // open: clr
  Register #(.width(5)) register_38 (.D(rt_EX), .en(1'b1), .clk(out_5), .Q(rt_MEM));  // open: clr
  Register #(.width(6)) register_39 (.D(Func_EX), .en(1'b1), .clk(out_5), .Q(Func_MEM));  // open: clr
  Register #(.width(5)) register_40 (.D(SHA_EX), .en(1'b1), .clk(out_5), .Q(SHA_MEM));  // open: clr
  Register #(.width(5)) register_41 (.D(rd_EX), .en(1'b1), .clk(out_5), .Q(rd_MEM));  // open: clr
  Register #(.width(32)) register_42 (.D(Imm_ext_EX), .en(1'b1), .clk(out_5), .Q(Imm_ext_MEM));  // open: clr
  Register #(.width(1)) register_43 (.D(Reg_Write_EX), .en(1'b1), .clk(out_5), .Q(Reg_Write_MEM));  // open: clr
  Register #(.width(1)) register_44 (.D(ALU_Src_EX), .en(1'b1), .clk(out_5), .Q(ALU_Src_MEM));  // open: clr
  Register #(.width(2)) register_45 (.D(PC_control_EX), .en(1'b1), .clk(out_5), .Q(PC_control_MEM));  // open: clr
  Register #(.width(2)) register_46 (.D(Reg_Dest_EX), .en(1'b1), .clk(out_5), .Q(Reg_Dest_MEM));  // open: clr
  Register #(.width(2)) register_47 (.D(Reg_Write_Sel_EX), .en(1'b1), .clk(out_5), .Q(Reg_Write_Sel_MEM));  // open: clr
  Register #(.width(2)) register_48 (.D(MEMW_Sel_EX), .en(1'b1), .clk(out_5), .Q(MEMW_Sel_MEM));  // open: clr
  Register #(.width(1)) register_49 (.D(Finish_EX), .en(1'b1), .clk(out_5), .Q(Finish_MEM));  // open: clr
  Register #(.width(32)) register_50 (.D(Read_Data1_EX), .en(1'b1), .clk(out_5), .Q(Read_Data1_MEM));  // open: clr
  Register #(.width(32)) register_51 (.D(Read_Data2_EX), .en(1'b1), .clk(out_5), .Q(Read_Data2_MEM));  // open: clr
  Register #(.width(1)) register_52 (.D(is_mem_inst_EX), .en(1'b1), .clk(out_5), .Q(is_mem_inst_MEM));  // open: clr
  Register #(.width(32)) register_53 (.D(ALU_Result_EX), .en(1'b1), .clk(out_5), .Q(ALU_Result_MEM));  // open: clr
  Register #(.width(2)) register_54 (.D(MEMW_Sel_EX), .en(1'b1), .clk(out_5), .Q(MEMW_Sel_MEM));  // open: clr
  Register #(.width(1)) register_55 (.D(Zero_EX), .en(1'b1), .clk(out_5), .Q(Zero_MEM));  // open: clr
  Register #(.trigger("falling"), .width(1)) register_56 (
    .D(is_mem_inst_MEM), .clk(out_5), .Q(is_mem_inst_MEM_secondary));  // open: en, clr
  Decoder #(.enable("false"), .select(2)) decoder_1 (
    .out0(decoder_1_out0[0]), .out1(decoder_1_out0[1]), .out2(decoder_1_out0[2]), .out3(decoder_1_out0[3]),
    .sel(ALU_Result_MEM[1:0]));
  not not_7 (not_7_out, out_4);
  Multiplexer #(.select(2), .width(4)) multiplexer_46 (
    .in0(4'b0000), .in1(4'b1111), .in2(decoder_1_out0), .in3(4'b0000), .out(multiplexer_46_out),
    .sel(MEMW_Sel_MEM));
  not not_8 (not_8_out, out_4);
  and and_8 (and_8_out, not_7_out, is_mem_inst_MEM);
  Counter #(.max('h12)) counter_3 (
    .clr(hit_MEM), .load(1'b0), .up(1'b1), .clk(and_8_out), .Q(miss_counter_state));  // open: count, D, carry
  Multiplexer #(.select(2), .width(5)) multiplexer_47 (
    .in0(rt_MEM), .in1(rd_MEM), .in2({5{1'b1}}), .in3(5'b00001), .out(Reg_Write_Target_MEM),
    .sel(Reg_Dest_MEM));
  Cache cache_1 (
    .memWriteData(Read_Data2_MEM), .memAddress(ALU_Result_MEM), .clk(not_8_out),
    .write_mask(multiplexer_46_out), .miss_counter_state(miss_counter_state), .main_mem_read_data(out_1),
    .is_mem_inst(is_mem_inst_MEM), .hit(hit_MEM), .cacheReadData(MemReadData_MEM),
    .write_back0_addr(cache_1_write_back0_addr), .write_back1_addr(cache_1_write_back1_addr),
    .write_back2_addr(cache_1_write_back2_addr), .write_back3_addr(cache_1_write_back3_addr),
    .fetch0_addr(cache_1_fetch0_addr), .fetch1_addr(cache_1_fetch1_addr), .fetch2_addr(cache_1_fetch2_addr),
    .fetch3_addr(cache_1_fetch3_addr), .write_back0_data(cache_1_write_back0_data),
    .write_back1_data(cache_1_write_back1_data), .write_back2_data(cache_1_write_back2_data),
    .write_back3_data(cache_1_write_back3_data), .wb_mask_select(cache_1_wb_mask_select));
  and and_9 (and_9_out, cache_1_wb_mask_select, mem_mask_sel);
  not not_9 (not_9_out, out_4);
  not not_10 (not_10_out, hit_MEM);
  Multiplexer #(.select(3), .width(32)) multiplexer_48 (
    .in0(cache_1_write_back0_addr), .in1(cache_1_write_back1_addr), .in2(cache_1_write_back2_addr),
    .in3(cache_1_write_back3_addr), .in4(cache_1_fetch0_addr), .in5(cache_1_fetch1_addr),
    .in6(cache_1_fetch2_addr), .in7(cache_1_fetch3_addr), .out(multiplexer_48_out), .sel(mem_addr_sel));
  Multiplexer #(.width(4)) multiplexer_49 (.in0(4'b0000), .in1(4'b1111), .out(multiplexer_49_out), .sel(and_9_out));
  Multiplexer #(.select(2), .width(32)) multiplexer_50 (
    .in0(cache_1_write_back0_data), .in1(cache_1_write_back1_data), .in2(cache_1_write_back2_data),
    .in3(cache_1_write_back3_data), .out(multiplexer_50_out), .sel(mem_data_sel));
  and and_10 (out_8, not_9_out, is_mem_inst_MEM, not_10_out);
  PLA #(.in_width(8), .out_width(7), .\table ("00000000 0001000 # w0_wb_addr\n00000001 0011001 # w1_wb_addr\n00000010 0101010 # w2 wb_addr\n00000011 0111011 # w3_wb_addr\n00000100 0000100 # w0_fetch_addr\n00000101 0000101 # w1_fetch_addr\n00000110 0000110 # w2_fetch_addr\n00000111 0000111 # w3_fetch_addr\n00010001 1000000 # mem_done")) miss_controls (
    .in(miss_counter_state), .out({mem_fetch_done, mem_data_sel, mem_mask_sel, mem_addr_sel}));
  memDelayed memdelayed_1 (
    .MemAddress(multiplexer_48_out), .MemWriteMask(multiplexer_49_out), .MemWriteData(multiplexer_50_out),
    .clk(out_8), .MemReadData(out_1));
  Register #(.width(1)) register_57 (.D(Predict_Taken_MEM), .en(1'b1), .clk(out_5), .Q(Predict_Taken_WB));  // open: clr
  Register #(.width(32)) register_58 (
    .D(Replace_Prediciton_MEM), .en(1'b1), .clk(out_5), .Q(Replace_Prediciton_WB));  // open: clr
  Register #(.width(32)) register_59 (.D(PC_MEM), .en(1'b1), .clk(out_5), .Q(PC_WB));  // open: clr
  Register #(.width(6)) register_60 (.D(opcode_MEM), .en(1'b1), .clk(out_5), .Q(opcode_WB));  // open: clr
  Register #(.width(5)) register_61 (.D(rs_MEM), .en(1'b1), .clk(out_5), .Q(rs_WB));  // open: clr
  Register #(.width(5)) register_62 (.D(rt_MEM), .en(1'b1), .clk(out_5), .Q(rt_WB));  // open: clr
  Register #(.width(6)) register_63 (.D(Func_MEM), .en(1'b1), .clk(out_5), .Q(Func_WB));  // open: clr
  Register #(.width(5)) register_64 (.D(SHA_MEM), .en(1'b1), .clk(out_5), .Q(SHA_WB));  // open: clr
  Register #(.width(5)) register_65 (.D(rd_MEM), .en(1'b1), .clk(out_5), .Q(rd_WB));  // open: clr
  Register #(.width(32)) register_66 (.D(Imm_ext_MEM), .en(1'b1), .clk(out_5), .Q(Imm_ext_WB));  // open: clr
  Register #(.width(1)) register_67 (.D(Reg_Write_MEM), .en(1'b1), .clk(out_5), .Q(Reg_Write_WB));  // open: clr
  Register #(.width(1)) register_68 (.D(ALU_Src_MEM), .en(1'b1), .clk(out_5), .Q(ALU_Src_WB));  // open: clr
  Register #(.width(2)) register_69 (.D(PC_control_MEM), .en(1'b1), .clk(out_5), .Q(PC_control_WB));  // open: clr
  Register #(.width(2)) register_70 (.D(Reg_Dest_MEM), .en(1'b1), .clk(out_5), .Q(Reg_Dest_WB));  // open: clr
  Register #(.width(2)) register_71 (.D(Reg_Write_Sel_MEM), .en(1'b1), .clk(out_5), .Q(Reg_Write_Sel_WB));  // open: clr
  Register #(.width(2)) register_72 (.D(MEMW_Sel_MEM), .en(1'b1), .clk(out_5), .Q(MEMW_Sel_WB));  // open: clr
  Register #(.width(1)) register_73 (.D(Finish_MEM), .en(1'b1), .clk(out_5), .Q(Finish_WB));  // open: clr
  Register #(.width(32)) register_74 (.D(Read_Data1_MEM), .en(1'b1), .clk(out_5), .Q(Read_Data1_WB));  // open: clr
  Register #(.width(32)) register_75 (.D(Read_Data2_MEM), .en(1'b1), .clk(out_5), .Q(Read_Data2_WB));  // open: clr
  Register #(.width(1)) register_76 (.D(is_mem_inst_MEM), .en(1'b1), .clk(out_5), .Q(is_mem_inst_WB));  // open: clr
  Register #(.width(32)) register_77 (.D(ALU_Result_MEM), .en(1'b1), .clk(out_5), .Q(ALU_Result_WB));  // open: clr
  Register #(.width(2)) register_78 (.D(MEMW_Sel_MEM), .en(1'b1), .clk(out_5), .Q(MEMW_Sel_WB));  // open: clr
  Register #(.width(1)) register_79 (.D(Zero_MEM), .en(1'b1), .clk(out_5), .Q(Zero_WB));  // open: clr
  Register #(.width(1)) register_80 (.D(hit_MEM), .en(1'b1), .clk(out_5), .Q(hit_WB));  // open: clr
  Register #(.width(32)) register_81 (.D(MemReadData_MEM), .en(1'b1), .clk(out_5), .Q(MemReadData_WB));  // open: clr

  // Other names for the same wires on the sheet: J_addr[5:0] = Func_IF; SHA_IF[4:0] = J_addr[10:6];
  //   rd_IF[4:0] = J_addr[15:11]; rt_IF[4:0] = J_addr[20:16]; rs_IF[4:0] = J_addr[25:21]; hit = out_7;
  //   is_mem_inst = out_3; PC[31:28] = J_value[31:28]; Main_Clock = out_4; main_mem_read_data[31:0] = out_1;
  //   MemReadData[31:0] = out_2; opcode[5:0] = out_6; reading_from_mem = out_8; Secondary_Clock = out_5

  // Notes on the sheet:
  //   PC Update
  //   branch pc update:
  //   PC Logic
  //   Next
  //   Jump
  //   <PC logic for normal and jump>(IF stage)
  //   <Stall logic for JR>
  //   <PC logic for branch>(EX stage output: MEM stage data)
  //   Clock
  //   IF
  //   Clk_Check
  //   ID
  //   Branch_Prediction
  //   EX
  //   Cache-memory
  //   MEM
  //   Handle data hazard target
  //   is_bit_valid
  //   Test_Outs
  //   WB
endmodule
