// Logisim project delayModule.circ as structural Verilog: 1 circuit, main circuit delayModule
module delayModule (
  input  [3:0] DataIn,
  input  clk,
  output [3:0] DataOut
);

  wire d_ff_1_q, d_ff_2_q, d_ff_3_q, d_ff_4_q, d_ff_5_q, d_ff_6_q, d_ff_7_q, d_ff_8_q, d_ff_9_q, d_ff_10_q,
       d_ff_11_q, d_ff_12_q, d_ff_13_q, d_ff_14_q, d_ff_15_q, d_ff_16_q;

  D_Flip_Flop d_ff_1 (.D(DataIn[0]), .clk(clk), .Q(d_ff_1_q));  // open: Qn, preset, reset
  D_Flip_Flop d_ff_2 (.D(DataIn[1]), .clk(clk), .Q(d_ff_2_q));  // open: Qn, preset, reset
  D_Flip_Flop d_ff_3 (.D(DataIn[2]), .clk(clk), .Q(d_ff_3_q));  // open: Qn, preset, reset
  D_Flip_Flop d_ff_4 (.D(DataIn[3]), .clk(clk), .Q(d_ff_4_q));  // open: Qn, preset, reset
  D_Flip_Flop d_ff_5 (.D(d_ff_1_q), .clk(clk), .Q(d_ff_5_q));  // open: Qn, preset, reset
  D_Flip_Flop d_ff_6 (.D(d_ff_2_q), .clk(clk), .Q(d_ff_6_q));  // open: Qn, preset, reset
  D_Flip_Flop d_ff_7 (.D(d_ff_3_q), .clk(clk), .Q(d_ff_7_q));  // open: Qn, preset, reset
  D_Flip_Flop d_ff_8 (.D(d_ff_4_q), .clk(clk), .Q(d_ff_8_q));  // open: Qn, preset, reset
  D_Flip_Flop d_ff_9 (.D(d_ff_5_q), .clk(clk), .Q(d_ff_9_q));  // open: Qn, preset, reset
  D_Flip_Flop d_ff_10 (.D(d_ff_6_q), .clk(clk), .Q(d_ff_10_q));  // open: Qn, preset, reset
  D_Flip_Flop d_ff_11 (.D(d_ff_7_q), .clk(clk), .Q(d_ff_11_q));  // open: Qn, preset, reset
  D_Flip_Flop d_ff_12 (.D(d_ff_8_q), .clk(clk), .Q(d_ff_12_q));  // open: Qn, preset, reset
  D_Flip_Flop d_ff_13 (.D(d_ff_9_q), .clk(clk), .Q(d_ff_13_q));  // open: Qn, preset, reset
  D_Flip_Flop d_ff_14 (.D(d_ff_10_q), .clk(clk), .Q(d_ff_14_q));  // open: Qn, preset, reset
  D_Flip_Flop d_ff_15 (.D(d_ff_11_q), .clk(clk), .Q(d_ff_15_q));  // open: Qn, preset, reset
  D_Flip_Flop d_ff_16 (.D(d_ff_12_q), .clk(clk), .Q(d_ff_16_q));  // open: Qn, preset, reset
  D_Flip_Flop d_ff_17 (.D(d_ff_13_q), .clk(clk), .Q(DataOut[0]));  // open: Qn, preset, reset
  D_Flip_Flop d_ff_18 (.D(d_ff_14_q), .clk(clk), .Q(DataOut[1]));  // open: Qn, preset, reset
  D_Flip_Flop d_ff_19 (.D(d_ff_15_q), .clk(clk), .Q(DataOut[2]));  // open: Qn, preset, reset
  D_Flip_Flop d_ff_20 (.D(d_ff_16_q), .clk(clk), .Q(DataOut[3]));  // open: Qn, preset, reset
endmodule
