// Logisim project l1_cache.circ as structural Verilog: 1 circuit, main circuit Cache
module Cache (
  input  [31:0] memWriteData,
  input  [31:0] memAddress,
  input  clk,
  input  [3:0] write_mask,
  input  [7:0] miss_counter_state,
  input  [31:0] main_mem_read_data,
  input  is_mem_inst,
  output hit,
  output [31:0] cacheReadData,
  output [31:0] write_back0_addr,
  output [31:0] write_back1_addr,
  output [31:0] write_back2_addr,
  output [31:0] write_back3_addr,
  output [31:0] fetch0_addr,
  output [31:0] fetch1_addr,
  output [31:0] fetch2_addr,
  output [31:0] fetch3_addr,
  output [31:0] write_back0_data,
  output [31:0] write_back1_data,
  output [31:0] write_back2_data,
  output [31:0] write_back3_data,
  output wb_mask_select
);

  wire and_1_out, and_2_out, and_3_out, block1_hit, comparator_1_eq, comparator_2_eq, LRU_Update0,
       LRU_Update1, LRU_Update2, LRU_Update3, multiplexer_2_out, multiplexer_4_out, multiplexer_24_out,
       multiplexer_26_out, not_1_out, not_2_out, not_3_out, not_4_out, or_1_out, pla_1_out, S0B0LRU, S0B0V,
       S0B1LRU, S0B1V, S1B0LRU, S1B0V, S1B1LRU, S1B1V, S2B0LRU, S2B0V, S2B1LRU, S2B1V, S3B0LRU, S3B0V,
       S3B1LRU, S3B1V, WE0, WE0_VT, WE1, WE1_VT, WE2, WE2_VT, WE3, WE3_VT, WE4, WE4_VT, WE5, WE5_VT, WE6,
       WE6_VT, WE7, WE7_VT, WE8, WE9, WE10, WE11, WE12, WE13, WE14, WE15, WE16, WE17, WE18, WE19, WE20, WE21,
       WE22, WE23, WE24, WE25, WE26, WE27, WE28, WE29, WE30, WE31;
  wire [0:0] block_select_bits, multiplexer_3_out;
  wire [1:0] multiplexer_6_out;
  wire [2:0] counter_w_sel_out;
  wire [2:2] multiplexer_5_out;
  wire [25:0] multiplexer_23_out, multiplexer_25_out, S0B0Tag, S0B1Tag, S1B0Tag, S1B1Tag, S2B0Tag, S2B1Tag,
       S3B0Tag, S3B1Tag;
  wire [31:0] B0W0, B0W1, B0W2, B0W3, B1W0, B1W1, B1W2, B1W3, B2W0, B2W1, B2W2, B2W3, B3W0, B3W1, B3W2, B3W3,
       B4W0, B4W1, B4W2, B4W3, B5W0, B5W1, B5W2, B5W3, B6W0, B6W1, B6W2, B6W3, B7W0, B7W1, B7W2, B7W3,
       multiplexer_7_out, multiplexer_8_out, multiplexer_9_out, multiplexer_10_out, multiplexer_11_out,
       multiplexer_12_out, multiplexer_13_out, multiplexer_14_out, multiplexer_15_out, multiplexer_16_out,
       multiplexer_17_out, multiplexer_18_out, write_data;

  Decoder #(.select(2)) decoder_1 (
    .out0(LRU_Update0), .out1(LRU_Update1), .out2(LRU_Update2), .out3(LRU_Update3), .sel(memAddress[5:4]),
    .en(and_1_out));
  and and_1 (and_1_out, hit, is_mem_inst);
  not not_1 (not_1_out, block1_hit);
  Register #(.width(1)) register_1 (.D(block1_hit), .en(LRU_Update0), .clk(clk), .Q(S0B0LRU));  // open: clr
  Register #(.width(1)) register_2 (.D(not_1_out), .en(LRU_Update0), .clk(clk), .Q(S0B1LRU));  // open: clr
  Register #(.width(1)) register_3 (.D(block1_hit), .en(LRU_Update1), .clk(clk), .Q(S1B0LRU));  // open: clr
  Register #(.width(1)) register_4 (.D(not_1_out), .en(LRU_Update1), .clk(clk), .Q(S1B1LRU));  // open: clr
  Register #(.width(1)) register_5 (.D(block1_hit), .en(LRU_Update2), .clk(clk), .Q(S2B0LRU));  // open: clr
  Register #(.width(1)) register_6 (.D(not_1_out), .en(LRU_Update2), .clk(clk), .Q(S2B1LRU));  // open: clr
  Register #(.width(1)) register_7 (.D(block1_hit), .en(LRU_Update2), .clk(clk), .Q(S3B0LRU));  // open: clr
  Register #(.width(1)) register_8 (.D(not_1_out), .en(LRU_Update2), .clk(clk), .Q(S3B1LRU));  // open: clr
  Multiplexer #(.width(32)) multiplexer_1 (.in0(main_mem_read_data), .in1(memWriteData), .out(write_data), .sel(hit));
  Register #(.width(1)) register_9 (.D(1'b1), .en(WE0_VT), .clk(clk), .Q(S0B0V));  // open: clr
  Register #(.width(1)) register_10 (.D(1'b1), .en(WE1_VT), .clk(clk), .Q(S0B1V));  // open: clr
  Register #(.width(1)) register_11 (.D(1'b1), .en(WE2_VT), .clk(clk), .Q(S1B0V));  // open: clr
  Register #(.width(1)) register_12 (.D(1'b1), .en(WE3_VT), .clk(clk), .Q(S1B1V));  // open: clr
  Register #(.width(1)) register_13 (.D(1'b1), .en(WE4_VT), .clk(clk), .Q(S2B0V));  // open: clr
  Register #(.width(1)) register_14 (.D(1'b1), .en(WE5_VT), .clk(clk), .Q(S2B1V));  // open: clr
  Register #(.width(1)) register_15 (.D(1'b1), .en(WE6_VT), .clk(clk), .Q(S3B0V));  // open: clr
  Register #(.width(1)) register_16 (.D(1'b1), .en(WE7_VT), .clk(clk), .Q(S3B1V));  // open: clr
  Register #(.width(26)) register_17 (.D(memAddress[31:6]), .en(WE0_VT), .clk(clk), .Q(S0B0Tag));  // open: clr
  Register #(.width(26)) register_18 (.D(memAddress[31:6]), .en(WE1_VT), .clk(clk), .Q(S0B1Tag));  // open: clr
  Register #(.width(26)) register_19 (.D(memAddress[31:6]), .en(WE2_VT), .clk(clk), .Q(S1B0Tag));  // open: clr
  Register #(.width(26)) register_20 (.D(memAddress[31:6]), .en(WE3_VT), .clk(clk), .Q(S1B1Tag));  // open: clr
  Register #(.width(26)) register_21 (.D(memAddress[31:6]), .en(WE4_VT), .clk(clk), .Q(S2B0Tag));  // open: clr
  Register #(.width(26)) register_22 (.D(memAddress[31:6]), .en(WE5_VT), .clk(clk), .Q(S2B1Tag));  // open: clr
  Register #(.width(26)) register_23 (.D(memAddress[31:6]), .en(WE6_VT), .clk(clk), .Q(S3B0Tag));  // open: clr
  Register #(.width(26)) register_24 (.D(memAddress[31:6]), .en(WE7_VT), .clk(clk), .Q(S3B1Tag));  // open: clr
  Multiplexer #(.select(2)) multiplexer_2 (
    .in0(S0B1LRU), .in1(S1B1LRU), .in2(S2B1LRU), .in3(S3B1LRU), .out(multiplexer_2_out), .sel(memAddress[5:4]));
  Multiplexer multiplexer_3 (.in0(block1_hit), .in1(multiplexer_2_out), .out(multiplexer_3_out[0]), .sel(not_2_out));
  not not_2 (not_2_out, hit);
  PLA #(.in_width(8), .out_width(3), .\table ("00001110 100 # w0_fetch\n00001111 101 # w1_fetch\n00010000 110 # w2_fetch\n00010001 111 # w3_fetch")) counter_w_sel (
    .in(miss_counter_state), .out(counter_w_sel_out));
  Register #(.width(32)) register_25 (.D(write_data), .en(WE3), .clk(clk), .Q(B0W3));  // open: clr
  Register #(.width(32)) register_26 (.D(write_data), .en(WE7), .clk(clk), .Q(B1W3));  // open: clr
  Register #(.width(32)) register_27 (.D(write_data), .en(WE11), .clk(clk), .Q(B2W3));  // open: clr
  Register #(.width(32)) register_28 (.D(write_data), .en(WE15), .clk(clk), .Q(B3W3));  // open: clr
  Register #(.width(32)) register_29 (.D(write_data), .en(WE19), .clk(clk), .Q(B4W3));  // open: clr
  Register #(.width(32)) register_30 (.D(write_data), .en(WE23), .clk(clk), .Q(B5W3));  // open: clr
  Register #(.width(32)) register_31 (.D(write_data), .en(WE27), .clk(clk), .Q(B6W3));  // open: clr
  Register #(.width(32)) register_32 (.D(write_data), .en(WE31), .clk(clk), .Q(B7W3));  // open: clr
  PLA #(.in_width(8), .out_width(1), .\table ("00010001 1 # update_tag_valid")) pla_1 (
    .in(miss_counter_state), .out(pla_1_out));
  Register #(.width(32)) register_33 (.D(write_data), .en(WE2), .clk(clk), .Q(B0W2));  // open: clr
  Register #(.width(32)) register_34 (.D(write_data), .en(WE6), .clk(clk), .Q(B1W2));  // open: clr
  Register #(.width(32)) register_35 (.D(write_data), .en(WE10), .clk(clk), .Q(B2W2));  // open: clr
  Register #(.width(32)) register_36 (.D(write_data), .en(WE14), .clk(clk), .Q(B3W2));  // open: clr
  Register #(.width(32)) register_37 (.D(write_data), .en(WE18), .clk(clk), .Q(B4W2));  // open: clr
  Register #(.width(32)) register_38 (.D(write_data), .en(WE22), .clk(clk), .Q(B5W2));  // open: clr
  Register #(.width(32)) register_39 (.D(write_data), .en(WE26), .clk(clk), .Q(B6W2));  // open: clr
  Register #(.width(32)) register_40 (.D(write_data), .en(WE30), .clk(clk), .Q(B7W2));  // open: clr
  Multiplexer #(.select(2)) multiplexer_4 (
    .in0(S0B1LRU), .in1(S1B1LRU), .in2(S2B1LRU), .in3(S3B1LRU), .out(multiplexer_4_out), .sel(memAddress[5:4]));
  Decoder #(.select(3)) decoder_2 (
    .out0(WE0_VT), .out1(WE1_VT), .out2(WE2_VT), .out3(WE3_VT), .out4(WE4_VT), .out5(WE5_VT), .out6(WE6_VT),
    .out7(WE7_VT), .sel({memAddress[5:4], multiplexer_3_out[0]}), .en(pla_1_out));
  Multiplexer multiplexer_5 (.in0(block1_hit), .in1(multiplexer_4_out), .out(multiplexer_5_out[2]), .sel(not_3_out));
  not not_3 (not_3_out, hit);
  Register #(.width(32)) register_41 (.D(write_data), .en(WE1), .clk(clk), .Q(B0W1));  // open: clr
  Register #(.width(32)) register_42 (.D(write_data), .en(WE5), .clk(clk), .Q(B1W1));  // open: clr
  Register #(.width(32)) register_43 (.D(write_data), .en(WE9), .clk(clk), .Q(B2W1));  // open: clr
  Register #(.width(32)) register_44 (.D(write_data), .en(WE13), .clk(clk), .Q(B3W1));  // open: clr
  Register #(.width(32)) register_45 (.D(write_data), .en(WE17), .clk(clk), .Q(B4W1));  // open: clr
  Register #(.width(32)) register_46 (.D(write_data), .en(WE21), .clk(clk), .Q(B5W1));  // open: clr
  Register #(.width(32)) register_47 (.D(write_data), .en(WE25), .clk(clk), .Q(B6W1));  // open: clr
  Register #(.width(32)) register_48 (.D(write_data), .en(WE29), .clk(clk), .Q(B7W1));  // open: clr
  Multiplexer #(.width(2)) multiplexer_6 (
    .in0(memAddress[3:2]), .in1(counter_w_sel_out[1:0]), .out(multiplexer_6_out), .sel(not_4_out));
  not not_4 (not_4_out, hit);
  Register #(.width(32)) register_49 (.D(write_data), .en(WE0), .clk(clk), .Q(B0W0));  // open: clr
  Register #(.width(32)) register_50 (.D(write_data), .en(WE4), .clk(clk), .Q(B1W0));  // open: clr
  Register #(.width(32)) register_51 (.D(write_data), .en(WE8), .clk(clk), .Q(B2W0));  // open: clr
  Register #(.width(32)) register_52 (.D(write_data), .en(WE12), .clk(clk), .Q(B3W0));  // open: clr
  Register #(.width(32)) register_53 (.D(write_data), .en(WE16), .clk(clk), .Q(B4W0));  // open: clr
  Register #(.width(32)) register_54 (.D(write_data), .en(WE20), .clk(clk), .Q(B5W0));  // open: clr
  Register #(.width(32)) register_55 (.D(write_data), .en(WE24), .clk(clk), .Q(B6W0));  // open: clr
  Register #(.width(32)) register_56 (.D(write_data), .en(WE28), .clk(clk), .Q(B7W0));  // open: clr
  Decoder #(.select(5)) decoder_3 (
    .out0(WE0), .out1(WE1), .out2(WE2), .out3(WE3), .out4(WE4), .out5(WE5), .out6(WE6), .out7(WE7),
    .out8(WE8), .out9(WE9), .out10(WE10), .out11(WE11), .out12(WE12), .out13(WE13), .out14(WE14),
    .out15(WE15), .out16(WE16), .out17(WE17), .out18(WE18), .out19(WE19), .out20(WE20), .out21(WE21),
    .out22(WE22), .out23(WE23), .out24(WE24), .out25(WE25), .out26(WE26), .out27(WE27), .out28(WE28),
    .out29(WE29), .out30(WE30), .out31(WE31),
    .sel({memAddress[5:4], multiplexer_5_out[2], multiplexer_6_out}), .en(or_1_out));
  or or_1 (or_1_out, write_mask[0], and_2_out);
  and and_2 (and_2_out, not_4_out, counter_w_sel_out[2]);
  Multiplexer #(.select(2), .width(32)) multiplexer_7 (
    .in0(B0W0), .in1(B0W1), .in2(B0W2), .in3(B0W3), .out(multiplexer_7_out), .sel(memAddress[3:2]));
  Multiplexer #(.select(2), .width(32)) multiplexer_8 (
    .in0(B1W0), .in1(B1W1), .in2(B1W2), .in3(B1W3), .out(multiplexer_8_out), .sel(memAddress[3:2]));
  Multiplexer #(.select(2), .width(32)) multiplexer_9 (
    .in0(B2W0), .in1(B2W1), .in2(B2W2), .in3(B2W3), .out(multiplexer_9_out), .sel(memAddress[3:2]));
  Multiplexer #(.select(2), .width(32)) multiplexer_10 (
    .in0(B3W0), .in1(B3W1), .in2(B3W2), .in3(B3W3), .out(multiplexer_10_out), .sel(memAddress[3:2]));
  Multiplexer #(.select(2), .width(32)) multiplexer_11 (
    .in0(B4W0), .in1(B4W1), .in2(B4W2), .in3(B4W3), .out(multiplexer_11_out), .sel(memAddress[3:2]));
  Multiplexer #(.select(2), .width(32)) multiplexer_12 (
    .in0(B5W0), .in1(B5W1), .in2(B5W2), .in3(B5W3), .out(multiplexer_12_out), .sel(memAddress[3:2]));
  Multiplexer #(.select(2), .width(32)) multiplexer_13 (
    .in0(B6W0), .in1(B6W1), .in2(B6W2), .in3(B6W3), .out(multiplexer_13_out), .sel(memAddress[3:2]));
  Multiplexer #(.select(2), .width(32)) multiplexer_14 (
    .in0(B7W0), .in1(B7W1), .in2(B7W2), .in3(B7W3), .out(multiplexer_14_out), .sel(memAddress[3:2]));
  Multiplexer #(.width(32)) multiplexer_15 (
    .in0(multiplexer_7_out), .in1(multiplexer_8_out), .out(multiplexer_15_out), .sel(block1_hit));
  Multiplexer #(.width(32)) multiplexer_16 (
    .in0(multiplexer_9_out), .in1(multiplexer_10_out), .out(multiplexer_16_out), .sel(block1_hit));
  Multiplexer #(.width(32)) multiplexer_17 (
    .in0(multiplexer_11_out), .in1(multiplexer_12_out), .out(multiplexer_17_out), .sel(block1_hit));
  Multiplexer #(.width(32)) multiplexer_18 (
    .in0(multiplexer_13_out), .in1(multiplexer_14_out), .out(multiplexer_18_out), .sel(block1_hit));
  Multiplexer #(.select(2), .width(32)) multiplexer_19 (
    .in0(multiplexer_15_out), .in1(multiplexer_16_out), .in2(multiplexer_17_out), .in3(multiplexer_18_out),
    .out(cacheReadData), .sel(memAddress[5:4]));
  Multiplexer #(.select(3), .width(32)) multiplexer_20 (
    .in0(B0W0), .in1(B1W0), .in2(B2W0), .in3(B3W0), .in4(B4W0), .in5(B5W0), .in6(B6W0), .in7(B7W0),
    .out(write_back0_data), .sel({memAddress[5:4], block_select_bits[0]}));
  Multiplexer #(.select(3), .width(32)) multiplexer_21 (
    .in0(B0W2), .in1(B1W2), .in2(B2W2), .in3(B3W2), .in4(B4W2), .in5(B5W2), .in6(B6W2), .in7(B7W2),
    .out(write_back2_data), .sel({memAddress[5:4], block_select_bits[0]}));
  Multiplexer #(.select(3)) multiplexer_22 (
    .in0(S0B0V), .in1(S0B1V), .in2(S1B0V), .in3(S1B1V), .in4(S2B0V), .in5(S2B1V), .in6(S3B0V), .in7(S3B1V),
    .out(wb_mask_select), .sel({memAddress[5:4], block_select_bits[0]}));
  Multiplexer #(.select(2), .width(26)) multiplexer_23 (
    .in0(S0B0Tag), .in1(S1B0Tag), .in2(S2B0Tag), .in3(S3B0Tag), .out(multiplexer_23_out),
    .sel(memAddress[5:4]));
  Multiplexer #(.select(2)) multiplexer_24 (
    .in0(S0B0V), .in1(S1B0V), .in2(S2B0V), .in3(S3B0V), .out(multiplexer_24_out), .sel(memAddress[5:4]));
  Multiplexer #(.select(2), .width(26)) multiplexer_25 (
    .in0(S0B1Tag), .in1(S1B1Tag), .in2(S2B1Tag), .in3(S3B1Tag), .out(multiplexer_25_out),
    .sel(memAddress[5:4]));
  Multiplexer #(.select(2)) multiplexer_26 (
    .in0(S0B1V), .in1(S1B1V), .in2(S2B1V), .in3(S3B1V), .out(multiplexer_26_out), .sel(memAddress[5:4]));
  Multiplexer #(.select(2)) multiplexer_27 (
    .in0(S0B1LRU), .in1(S1B1LRU), .in2(S2B1LRU), .in3(S3B1LRU), .out(block_select_bits[0]),
    .sel(memAddress[5:4]));
  Comparator #(.width(26)) comparator_1 (
    .a(memAddress[31:6]), .b(multiplexer_23_out), .eq(comparator_1_eq));  // open: gt, lt
  Comparator #(.width(26)) comparator_2 (
    .a(memAddress[31:6]), .b(multiplexer_25_out), .eq(comparator_2_eq));  // open: gt, lt
  Multiplexer #(.select(3), .width(26)) multiplexer_28 (
    .in0(S0B0Tag), .in1(S0B1Tag), .in2(S1B0Tag), .in3(S1B1Tag), .in4(S2B0Tag), .in5(S2B1Tag), .in6(S3B0Tag),
    .in7(S3B1Tag), .out(write_back0_addr[31:6]), .sel({memAddress[5:4], block_select_bits[0]}));
  and and_3 (and_3_out, comparator_1_eq, multiplexer_24_out);
  and and_4 (block1_hit, comparator_2_eq, multiplexer_26_out);
  Multiplexer #(.select(3), .width(32)) multiplexer_29 (
    .in0(B0W1), .in1(B1W1), .in2(B2W1), .in3(B3W1), .in4(B4W1), .in5(B5W1), .in6(B6W1), .in7(B7W1),
    .out(write_back1_data), .sel({memAddress[5:4], block_select_bits[0]}));
  Multiplexer #(.select(3), .width(32)) multiplexer_30 (
    .in0(B0W3), .in1(B1W3), .in2(B2W3), .in3(B3W3), .in4(B4W3), .in5(B5W3), .in6(B6W3), .in7(B7W3),
    .out(write_back3_data), .sel({memAddress[5:4], block_select_bits[0]}));
  or or_2 (hit, and_3_out, block1_hit);

  assign fetch0_addr = {memAddress[31:4], 4'b0000};
  assign fetch1_addr = {memAddress[31:4], 4'b0100};
  assign fetch2_addr = {memAddress[31:4], 4'b1000};
  assign fetch3_addr = {memAddress[31:4], 4'b1100};
  assign write_back0_addr[5:0] = {memAddress[5:4], 4'b0000};
  assign write_back1_addr = {write_back0_addr[31:6], memAddress[5:4], 4'b0100};
  assign write_back2_addr = {write_back0_addr[31:6], memAddress[5:4], 4'b1000};
  assign write_back3_addr = {write_back0_addr[31:6], memAddress[5:4], 4'b1100};

  // Other names for the same wires on the sheet: counter_state[7:0] = miss_counter_state;
  //   block_select_bits[2:1] = memAddress[5:4]; set[1:0] = memAddress[5:4]; tag[25:0] = memAddress[31:6];
  //   mem_read_data[31:0] = main_mem_read_data; word[1:0] = memAddress[3:2]; read_result[31:0] = cacheReadData;
  //   WE = write_mask[0]

  // Notes on the sheet:
  //   Inputs
  //   Set 0
  //   Set 1
  //   Set 2
  //   Set 3
  //   data fetched from main memory
  //   LRU Bit
  //   Valid Bit
  //   Tag
  //   write_enable_select_logic
  //   Outputs
  //   Delayed Mem inputs
endmodule
