// Logisim project memDelayed.circ as structural Verilog: 1 circuit, main circuit memDelayed
module memDelayed (
  input  [31:0] MemAddress,
  input  [3:0] MemWriteMask,
  input  [31:0] MemWriteData,
  input  clk,
  output [31:0] MemReadData
);

  wire [3:0] delaymodule_1_dataout, delaymodule_2_dataout, delaymodule_3_dataout, delaymodule_4_dataout,
       delaymodule_5_dataout, delaymodule_6_dataout, delaymodule_7_dataout, delaymodule_8_dataout,
       delaymodule_9_dataout, delaymodule_10_dataout, delaymodule_11_dataout, delaymodule_12_dataout,
       delaymodule_13_dataout, delaymodule_14_dataout, delaymodule_15_dataout, delaymodule_16_dataout,
       delaymodule_17_dataout;
  wire [7:0] DMEM_0_dout, DMEM_1_dout, DMEM_2_dout, DMEM_3_dout;

  delayModule delaymodule_1 (.DataIn(MemWriteData[3:0]), .clk(clk), .DataOut(delaymodule_1_dataout));
  delayModule delaymodule_2 (.DataIn(MemWriteData[7:4]), .clk(clk), .DataOut(delaymodule_2_dataout));
  delayModule delaymodule_3 (.DataIn(MemWriteData[11:8]), .clk(clk), .DataOut(delaymodule_3_dataout));
  delayModule delaymodule_4 (.DataIn(MemWriteData[15:12]), .clk(clk), .DataOut(delaymodule_4_dataout));
  delayModule delaymodule_5 (.DataIn(MemWriteData[19:16]), .clk(clk), .DataOut(delaymodule_5_dataout));
  delayModule delaymodule_6 (.DataIn(MemWriteData[23:20]), .clk(clk), .DataOut(delaymodule_6_dataout));
  delayModule delaymodule_7 (.DataIn(MemWriteData[27:24]), .clk(clk), .DataOut(delaymodule_7_dataout));
  delayModule delaymodule_8 (.DataIn(MemWriteData[31:28]), .clk(clk), .DataOut(delaymodule_8_dataout));
  delayModule delaymodule_9 (.DataIn(MemAddress[3:0]), .clk(clk), .DataOut(delaymodule_9_dataout));
  delayModule delaymodule_10 (.DataIn(MemAddress[7:4]), .clk(clk), .DataOut(delaymodule_10_dataout));
  delayModule delaymodule_11 (.DataIn(MemAddress[11:8]), .clk(clk), .DataOut(delaymodule_11_dataout));
  delayModule delaymodule_12 (.DataIn(MemAddress[15:12]), .clk(clk), .DataOut(delaymodule_12_dataout));
  delayModule delaymodule_13 (.DataIn(MemAddress[19:16]), .clk(clk), .DataOut(delaymodule_13_dataout));
  delayModule delaymodule_14 (.DataIn(MemAddress[23:20]), .clk(clk), .DataOut(delaymodule_14_dataout));
  delayModule delaymodule_15 (.DataIn(MemAddress[27:24]), .clk(clk), .DataOut(delaymodule_15_dataout));
  delayModule delaymodule_16 (.DataIn(MemAddress[31:28]), .clk(clk), .DataOut(delaymodule_16_dataout));
  delayModule delaymodule_17 (.DataIn(MemWriteMask), .clk(clk), .DataOut(delaymodule_17_dataout));
  RAM #(.addrWidth(14)) DMEM_0 (
    .addr({delaymodule_12_dataout, delaymodule_11_dataout, delaymodule_10_dataout, delaymodule_9_dataout[3:2]}),
    .we(delaymodule_17_dataout[0]), .oe(1'b1), .clk(clk),
    .din({delaymodule_2_dataout, delaymodule_1_dataout}), .dout(DMEM_0_dout));
  RAM #(.addrWidth(14)) DMEM_1 (
    .addr({delaymodule_12_dataout, delaymodule_11_dataout, delaymodule_10_dataout, delaymodule_9_dataout[3:2]}),
    .we(delaymodule_17_dataout[1]), .oe(1'b1), .clk(clk),
    .din({delaymodule_4_dataout, delaymodule_3_dataout}), .dout(DMEM_1_dout));
  RAM #(.addrWidth(14)) DMEM_2 (
    .addr({delaymodule_12_dataout, delaymodule_11_dataout, delaymodule_10_dataout, delaymodule_9_dataout[3:2]}),
    .we(delaymodule_17_dataout[2]), .oe(1'b1), .clk(clk),
    .din({delaymodule_6_dataout, delaymodule_5_dataout}), .dout(DMEM_2_dout));
  RAM #(.addrWidth(14)) DMEM_3 (
    .addr({delaymodule_12_dataout, delaymodule_11_dataout, delaymodule_10_dataout, delaymodule_9_dataout[3:2]}),
    .we(delaymodule_17_dataout[3]), .oe(1'b1), .clk(clk),
    .din({delaymodule_8_dataout, delaymodule_7_dataout}), .dout(DMEM_3_dout));
  delayModuleOut delaymoduleout_1 (.DataIn(DMEM_0_dout[3:0]), .clk(clk), .DataOut(MemReadData[3:0]));
  delayModuleOut delaymoduleout_2 (.DataIn(DMEM_0_dout[7:4]), .clk(clk), .DataOut(MemReadData[7:4]));
  delayModuleOut delaymoduleout_3 (.DataIn(DMEM_1_dout[3:0]), .clk(clk), .DataOut(MemReadData[11:8]));
  delayModuleOut delaymoduleout_4 (.DataIn(DMEM_1_dout[7:4]), .clk(clk), .DataOut(MemReadData[15:12]));
  delayModuleOut delaymoduleout_5 (.DataIn(DMEM_2_dout[3:0]), .clk(clk), .DataOut(MemReadData[19:16]));
  delayModuleOut delaymoduleout_6 (.DataIn(DMEM_2_dout[7:4]), .clk(clk), .DataOut(MemReadData[23:20]));
  delayModuleOut delaymoduleout_7 (.DataIn(DMEM_3_dout[3:0]), .clk(clk), .DataOut(MemReadData[27:24]));
  delayModuleOut delaymoduleout_8 (.DataIn(DMEM_3_dout[7:4]), .clk(clk), .DataOut(MemReadData[31:28]));
endmodule
