// Logisim project alu_test.circ as structural Verilog: 1 circuit, main circuit alu_test
module alu_test (
  input  [31:0] in1,
  input  [31:0] in2,
  input  [5:0] func,
  input  [5:0] opcode,
  input  [4:0] SHA,
  output zero,
  output [31:0] Res
);

  wire alu_control_unit_1_p3;
  wire [1:0] alu_control_unit_1_p4;
  wire [4:0] multiplexer_1_out;

  // alu_control_unit alu_control_unit_1: pin names not known; wires that end beside it: func, opcode, alu_control_unit_1_p3, alu_control_unit_1_p4
  Multiplexer #(.select(2), .width(5)) multiplexer_1 (
    .in0(SHA), .in1(in1[4:0]), .in2(5'b10000), .in3({5{1'b0}}), .out(multiplexer_1_out),
    .sel(alu_control_unit_1_p4));
  // ALU alu_1: pin names not known; wires that end beside it: in1, in2, alu_control_unit_1_p3, multiplexer_1_out, zero, Res
endmodule
