// Logisim project control_unit_test.circ as structural Verilog: 1 circuit, main circuit test_cu
module test_cu (
  input  [5:0] OpCode,
  input  [5:0] Func,
  output out_3,
  output out_4,
  output [1:0] out_5,
  output [1:0] out_6,
  output [1:0] out_7,
  output [1:0] out_8
);

  control_unit control_unit_1 (
    .opcode(OpCode), .func(Func), .Reg_Write(out_3), .ALU_Src(out_4), .PC_control(out_5),
    .Reg_Dest_Sel(out_6), .Reg_Write_Sel(out_7), .MEMW_Sel(out_8));

  // Other names for the same wires on the sheet: Func_Tun[5:0] = Func; OpCode_Tun[5:0] = OpCode

  // Notes on the sheet:
  //   Input
  //   Test Component
endmodule
